# Fritzing sketch arduino-oving-4 (saved by Fritzing 0.9.3b)
breadboards: 1

parts:
  Part1 = Bluetooth HC-05 Macho
  Part4 = Arduino Uno (Rev3)
  LED1 = smd LED [color="Red (633nm)" package="0805 [SMD]"]
  R1 = Resistor [tolerance=±5% resistance=220 package="2512 [SMD]"]

nets:
  N1: Part1.TXD, Part4.A5/SCL
  N2: Part1.RXD, Part4.A4/SDA
  VCC: Part1.VCC, Part4.5V
  GND: Part1.GND, Part4.GND, LED1.cathode
  N3: Part4.A1, R1.Pin_1
  N4: LED1.anode, R1.Pin_0
